# Fritzing sketch VoltimetrINO (saved by Fritzing 0.9.3b)
breadboards: 1

parts:
  LCD1 = LCD screen  # not connected
  ZS-042_RTC1 = ZS-042 RTC Module
  Componente1 = Arduino Nano (Rev3.0) (ICSP)
  R1 = Resistor [tolerance=±5% resistance=220 package=THT]
  R2 = Resistor [tolerance=±5% resistance=220 package=THT]

nets:
  VCC: ZS-042_RTC1.VCC, Componente1.5V
  N1: ZS-042_RTC1.SDA, Componente1.A4
  N2: ZS-042_RTC1.SCL, Componente1.A5
  N3: Componente1.A0, R1.Pin_1, R2.Pin_0

notes:
  +
  a questi due cavi va collegata la batteria da testare
  -
  TABELLA RESISTENZE
  Voltaggio massimo R1 R2 Valore "resistorFactor"
  5V V+ pin A0 / 1023
  10V 1Kohm 1Kohm 511
  15V 2Kohm 1Kohm 341
  20V 3Kohm 1Kohm 255
  30V 5Kohm 1Kohm 170
  Progetti & Tutorial Arduino
  R1
  R2
